// Digital circuit Branch.dig as structural Verilog
module Branch (
  input  r1data,
  input  r2data,
  input  brinst,
  input  [31:0] \type ,
  input  ubrinst,
  output rs1_pc,
  output pc_jump,
  output eq,
  output lt,
  output ge,
  output ltu,
  output geu
);

  wire and_1_out, and_2_out, and_3_out, and_4_out, and_5_out, and_6_out, bge_eq, blt_eq, bltu_2_eq,
       bltu_3_eq, bltu_eq, bne_eq, equ, gt, gtu, multiplexer_1_out, multiplexer_2_out, multiplexer_3_out,
       multiplexer_4_out, multiplexer_5_out, multiplexer_6_out, ne;

  Comparator comparator_1 (.a(r1data), .b(r2data), .gt(gtu), .eq(equ), .lt(ltu));
  Comparator comparator_2 (.a(r1data), .b(r2data), .gt(gt), .eq(eq), .lt(lt));
  or or_1 (ge, gt, eq);
  not not_1 (ne, eq);
  or or_2 (geu, gtu, equ);
  Comparator #(.Bits(32)) bltu (.a(32'h7), .b(\type ), .eq(bltu_eq));  // open: gt, lt
  Comparator #(.Bits(32)) bltu_2 (.a(32'h6), .b(\type ), .eq(bltu_2_eq));  // open: gt, lt
  Comparator #(.Bits(32)) bge (.a(32'h5), .b(\type ), .eq(bge_eq));  // open: gt, lt
  Comparator #(.Bits(32)) blt (.a(32'h4), .b(\type ), .eq(blt_eq));  // open: gt, lt
  Comparator #(.Bits(32)) bne (.a(32'h1), .b(\type ), .eq(bne_eq));  // open: gt, lt
  Comparator #(.Bits(32)) bltu_3 (.a({32{1'b0}}), .b(\type ), .eq(bltu_3_eq));  // open: gt, lt
  and and_1 (and_1_out, geu, bltu_eq);
  and and_2 (and_2_out, ltu, bltu_2_eq);
  and and_3 (and_3_out, ge, bge_eq);
  and and_4 (and_4_out, lt, blt_eq);
  and and_5 (and_5_out, ne, bne_eq);
  and and_6 (and_6_out, eq, bltu_3_eq);
  Multiplexer multiplexer_1 (.sel(and_1_out), .in_0(1'b0), .in_1(1'b1), .out(multiplexer_1_out));
  Multiplexer multiplexer_2 (.sel(and_2_out), .in_0(multiplexer_1_out), .in_1(1'b1), .out(multiplexer_2_out));
  Multiplexer multiplexer_3 (.sel(and_3_out), .in_0(multiplexer_2_out), .in_1(1'b1), .out(multiplexer_3_out));
  Multiplexer multiplexer_4 (.sel(and_4_out), .in_0(multiplexer_3_out), .in_1(1'b1), .out(multiplexer_4_out));
  Multiplexer multiplexer_5 (.sel(and_5_out), .in_0(multiplexer_4_out), .in_1(1'b1), .out(multiplexer_5_out));
  Multiplexer multiplexer_6 (.sel(and_6_out), .in_0(multiplexer_5_out), .in_1(1'b1), .out(multiplexer_6_out));
  and and_7 (rs1_pc, brinst, multiplexer_6_out);
  or or_3 (pc_jump, ubrinst, rs1_pc);
endmodule
