// Digital circuit Control- (2).dig as structural Verilog
module Control___2 (
  input  [31:0] INST,
  output imm_reg,
  output rfwen,
  output [2:0] func3,
  output [6:0] srai_sub,
  output [6:0] funct7,
  output [6:0] opcode,
  output [1:0] WBSel,
  output dmwen,
  output JAL_JALR,
  output store,
  output branch,
  output load
);

  wire JAL_eq, JALR_eq, Load_eq, or_3_out;
  wire [1:0] multiplexer_2_out;
  wire [2:0] parte_inicial___control_1_funct3;

  Parte_inicial___control parte_inicial___control_1 (
    .Inst(INST), .opcode(opcode), .funct3(parte_inicial___control_1_funct3), .funct7(funct7));  // open: rd, rs1, rs2
  Comparator #(.Bits(7)) R (.a(opcode), .b(7'b0110011), .eq(JAL_JALR));  // open: gt, lt
  Comparator #(.Bits(7)) I (.a(opcode), .b(7'b0010011), .eq(load));  // open: gt, lt
  Comparator #(.Bits(7)) S (.a(opcode), .b(7'b0100011), .eq(dmwen));  // open: gt, lt
  Comparator #(.Bits(7)) u_Load (.a(opcode), .b(7'b0000011), .eq(Load_eq));  // open: gt, lt
  Comparator #(.Bits(7)) JAL (.a(opcode), .b(7'b1101111), .eq(JAL_eq));  // open: gt, lt
  Comparator #(.Bits(7)) JALR (.a(opcode), .b(7'b1100111), .eq(JALR_eq));  // open: gt, lt
  Comparator #(.Bits(7)) u_Store (.a(opcode), .b(7'b0100011), .eq(store));  // open: gt, lt
  Comparator #(.Bits(7)) Load_2 (.a(opcode), .b(7'b0000011), .eq(load));  // open: gt, lt
  Comparator #(.Bits(7)) u_Branch (.a(opcode), .b(7'b1100011), .eq(branch));  // open: gt, lt
  not not_1 (imm_reg, JAL_JALR);
  or or_1 (JAL_JALR, JAL_eq, JALR_eq);
  Multiplexer #(.Bits(3)) multiplexer_1 (
    .sel(branch), .in_0(parte_inicial___control_1_funct3), .in_1(3'b000), .out(func3));
  or or_2 (rfwen, JAL_JALR, load);
  or or_3 (or_3_out, JAL_JALR, load);
  Multiplexer #(.Bits(2)) multiplexer_2 (.sel(JAL_JALR), .in_0(2'b00), .in_1(2'b10), .out(multiplexer_2_out));
  Multiplexer #(.Bits(7)) multiplexer_3 (.sel(or_3_out), .in_0(funct7), .in_1({7{1'b0}}), .out(srai_sub));
  Multiplexer #(.Bits(2)) multiplexer_4 (.sel(Load_eq), .in_0(multiplexer_2_out), .in_1(2'b01), .out(WBSel));
endmodule
