// Digital circuit Control.dig as structural Verilog
module Control (
  input  [31:0] Inst,
  output [6:0] opcode,
  output [4:0] rd,
  output [2:0] funct3,
  output [4:0] rs1,
  output [4:0] rs2,
  output [6:0] funct7,
  output [31:0] imm_i,
  output [4:0] sham_i,
  output srai_srli,
  output [31:0] imm_s,
  output [31:0] imm_b,
  output [31:0] imm_j,
  output [31:0] imm_u
);

  BitExtender #(.inputBits(1), .outputBits(20)) bitextender_1 (.in(Inst[31]), .out(imm_i[31:12]));
  BitExtender #(.inputBits(1), .outputBits(20)) bitextender_2 (.in(Inst[31]), .out(imm_s[31:12]));
  BitExtender #(.inputBits(1), .outputBits(19)) bitextender_3 (.in(Inst[31]), .out(imm_b[31:13]));
  BitExtender #(.inputBits(1), .outputBits(11)) bitextender_4 (.in(Inst[31]), .out(imm_j[31:21]));
  BitExtender #(.inputBits(1), .outputBits(12)) bitextender_5 (.in(1'b0), .out(imm_u[11:0]));

  assign funct3 = Inst[14:12];
  assign funct7 = Inst[31:25];
  assign imm_b[12:0] = {Inst[31], Inst[7], Inst[30:25], Inst[11:8], 1'b0};
  assign imm_i[11:0] = Inst[31:20];
  assign imm_j[20:0] = {Inst[31], Inst[19:12], Inst[20], Inst[30:21], 1'b0};
  assign imm_s[11:0] = {Inst[31:25], Inst[11:7]};
  assign imm_u[31:12] = Inst[31:12];
  assign opcode = Inst[6:0];
  assign rd = Inst[11:7];
  assign rs1 = Inst[19:15];
  assign rs2 = Inst[24:20];
  assign sham_i = Inst[24:20];
  assign srai_srli = Inst[30];
endmodule
