// Digital circuit Parte inicial - control.dig as structural Verilog
module Parte_inicial___control (
  input  [31:0] Inst,
  output [6:0] opcode,
  output [4:0] rd,
  output [2:0] funct3,
  output [4:0] rs1,
  output [4:0] rs2,
  output [6:0] funct7
);


  assign funct3 = Inst[14:12];
  assign funct7 = Inst[31:25];
  assign opcode = Inst[6:0];
  assign rd = Inst[11:7];
  assign rs1 = Inst[19:15];
  assign rs2 = Inst[24:20];
endmodule
