// Digital circuit ProgramCounter.dig as structural Verilog
module ProgramCounter (
  input  [31:0] \input ,
  input  inc,
  input  load,
  input  reset,
  input  clock,
  output [31:0] Output
);

  wire or_1_out;
  wire [31:0] add_1_s, multiplexer_1_out, multiplexer_2_out, multiplexer_3_out;

  Multiplexer #(.Bits(32)) multiplexer_1 (.sel(inc), .in_0(Output), .in_1(add_1_s), .out(multiplexer_1_out));
  Multiplexer #(.Bits(32)) multiplexer_2 (
    .sel(load), .in_0(multiplexer_1_out), .in_1(\input ), .out(multiplexer_2_out));
  Multiplexer #(.Bits(32)) multiplexer_3 (
    .sel(reset), .in_0(multiplexer_2_out), .in_1({32{1'b0}}), .out(multiplexer_3_out));
  or or_1 (or_1_out, inc, load, reset);
  Register #(.Bits(32)) register_1 (.D(multiplexer_3_out), .C(clock), .en(or_1_out), .Q(Output));
  Add #(.Bits(32)) add_1 (.a(Output), .b(32'h1), .c_i(1'b0), .s(add_1_s));  // open: c_o
endmodule
