// Digital circuit alu (1).dig as structural Verilog
module alu__1 (
  input  [2:0] f3,
  input  [31:0] op_1,
  input  [2:0] f7,
  input  [31:0] op_2,
  output [31:0] out
);

  wire [0:0] slt, sltu;
  wire [31:0] add, \and , \or , sll, sra, srl, sub, \xor ;

  Add #(.Bits(32)) add_1 (.a(op_1), .b(op_2), .c_i(1'b0), .s(add));  // open: c_o
  Sub #(.Bits(32)) sub_1 (.a(op_1), .b(op_2), .c_i(1'b0), .s(sub));  // open: c_o
  assign \xor  = op_1 ^ op_2;  // XOr xor_1, 32 bits wide
  assign \or  = op_1 | op_2;  // Or or_1, 32 bits wide
  assign \and  = op_1 & op_2;  // And and_1, 32 bits wide
  BarrelShifter #(.Bits(32)) u_sll (.in(op_1), .shift(op_2[5:0]), .out(sll));
  BarrelShifter #(.Bits(32), .direction("right")) u_srl (.in(op_1), .shift(op_2[5:0]), .out(srl));
  BarrelShifter #(.barrelShifterMode("arithmetic"), .Bits(32)) u_sra (.in(op_1), .shift(op_2[5:0]), .out(sra));
  Comparator #(.Signed("true"), .Bits(32)) u_slt (.a(op_1), .b(op_2), .lt(slt[0]));  // open: gt, eq
  Comparator #(.Bits(32)) u_sltu (.a(op_1), .b(op_2), .lt(sltu[0]));  // open: gt, eq
  Multiplexer #(.Selector_Bits(3), .Bits(32)) multiplexer_1 (
    .sel(f7), .in_0(add), .in_1(sll), .in_2(sub), .in_3({31'h1, slt[0]}), .in_4({{31{1'b0}}, sltu[0]}),
    .in_5(sra), .in_6(\or ), .in_7(srl), .out(out));
  // Probe bin on out
  // Probe dec on out
  // Probe hex on out
endmodule
