// Digital circuit instdecoder.dig as structural Verilog
module instdecoder (
  input  [31:0] Inst,
  output [6:0] Opcode,
  output [4:0] Rd,
  output [4:0] Rs1,
  output [4:0] Rs2
);


  assign Opcode = Inst[6:0];
  assign Rd = Inst[11:7];
  assign Rs1 = Inst[19:15];
  assign Rs2 = Inst[24:20];
endmodule
