// Digital circuit unitimm.dig as structural Verilog
module unitimm (
  input  [31:0] Inst,
  output [31:0] Imm
);

  wire [2:0] notconnected_4_out;
  wire [11:0] Imm_U;
  wire [31:0] notconnected_1_out, notconnected_2_out, notconnected_3_out;
  wire [31:12] Imm_I;
  wire [31:13] Imm_B;
  wire [31:21] Imm_S;

  BitExtender #(.inputBits(1), .outputBits(12)) bitextender_1 (.in(1'b0), .out(Imm_U));
  BitExtender #(.inputBits(1), .outputBits(11)) bitextender_2 (.in(Inst[31]), .out(Imm_S));
  BitExtender #(.inputBits(1), .outputBits(20)) bitextender_3 (.in(Inst[31]), .out(Imm_I));
  BitExtender #(.inputBits(1), .outputBits(20)) bitextender_4 (.in(Inst[31]), .out({Imm_S, Inst[31], Inst[19:12]}));
  BitExtender #(.inputBits(1), .outputBits(19)) bitextender_5 (.in(Inst[31]), .out(Imm_B));
  Multiplexer #(.Selector_Bits(3), .Bits(32)) multiplexer_1 (
    .sel(notconnected_4_out), .in_0({Imm_I, Inst[31:21], Inst[31]}),
    .in_1({Imm_S, Inst[31], Inst[19:12], Inst[31:21], Inst[7]}),
    .in_2({Imm_B, Inst[31], Inst[7], Inst[30:21], 1'b0}), .in_3({Inst[31:21], Inst[31], Inst[19:12], Imm_U}),
    .in_4({Imm_S, Inst[31], Inst[19:12], Inst[31:21], Inst[7]}), .in_5(notconnected_1_out),
    .in_6(notconnected_2_out), .in_7(notconnected_3_out), .out(Imm));
  // NotConnected on notconnected_1_out
  // NotConnected on notconnected_2_out
  // NotConnected on notconnected_3_out
  // NotConnected on notconnected_4_out

  assign {Inst[20], Inst[11:8]} = {Inst[31], Inst[24:21]};
  // also tied to GND on the sheet: Inst[7]

  // Other names for the same wires on the sheet: Imm_B[12:1] = {Inst[31], Inst[7], Inst[30:21]};
  //   Imm_S[20:0] = {Inst[31], Inst[19:12], Inst[31:21], Inst[7]};
  //   Imm_U[31:12] = {Inst[31:21], Inst[31], Inst[19:12]}; Imm_I[11:0] = {Inst[31:21], Inst[31]};
  //   shamt_I[4:0] = {Inst[24:21], Inst[31]}
endmodule
